# Fritzing sketch RAMPS-TMC2130-connection board (saved by Fritzing 0.9.3b)
circuit board: 3cm x 2.5cm
stripboards: 1

parts:
  J5 = male pin header, 4 pins [form="♂ (male)"]
  J3 = male pin header, 4 pins [form="♂ (male)"]
  J2 = male pin header, 4 pins [form="♂ (male)"]
  J4 = male pin header, 4 pins [form="♂ (male)"]
  J1 = shrouded pin header, 10 pins [form="♂ (shrouded male)"]
  J6 = male pin header, 4 pins [form="♂ (male)"]

nets:
  N1: J5.pin1, J1.pin1
  N2: J5.pin2, J3.pin2, J2.pin2, J4.pin2, J1.pin7, J6.pin2
  N3: J5.pin3, J3.pin3, J2.pin3, J4.pin3, J1.pin6, J6.pin3
  N4: J5.pin4, J3.pin4, J2.pin4, J4.pin4, J1.pin5, J6.pin4
  N5: J3.pin1, J1.pin9
  N6: J2.pin1, J1.pin8
  N7: J4.pin1, J1.pin10
  N8: J1.pin2, J6.pin1

notes:
  JTa
  2018
  E1
  E0
  Z
  Y
  X
